// Logisim project lab01_65070159.circ as structural Verilog: 5 circuits, main circuit main
module main (
  input  B0,
  input  B1,
  input  B2,
  input  B3,
  input  A0,
  input  A1,
  input  A2,
  input  A3,
  output out_9
);

  _4_bit_comparator u_4_bit_comparator_1 (
    .B0(B0), .B1(B1), .B2(B2), .B3(B3), .A0(A0), .A1(A1), .A2(A2), .A3(A3), .out_9(out_9));
endmodule

module XOR (
  input  A,
  input  B,
  output out_3
);

  wire and_1_out, and_2_out, not_1_out, not_2_out;

  not not_1 (not_1_out, A);
  not not_2 (not_2_out, B);
  and and_1 (and_1_out, B, not_1_out);
  and and_2 (and_2_out, not_2_out, A);
  or or_1 (out_3, and_1_out, and_2_out);
endmodule

module myXOR (
  input  B0,
  input  B1,
  input  B2,
  input  B3,
  input  B4,
  input  B5,
  output out_7
);

  wire xor_1_out_3, xor_2_out_3, xor_3_out_3, xor_4_out_3;

  XOR xor_1 (.A(B1), .B(B0), .out_3(xor_1_out_3));
  XOR xor_2 (.A(B3), .B(B2), .out_3(xor_2_out_3));
  XOR xor_3 (.A(B4), .B(B4), .out_3(xor_3_out_3));
  XOR xor_4 (.A(xor_2_out_3), .B(xor_1_out_3), .out_3(xor_4_out_3));
  XOR xor_5 (.A(xor_3_out_3), .B(xor_4_out_3), .out_3(out_7));
endmodule

module MyXNOR (
  input  A,
  input  B,
  output out_3
);

  wire and_1_out, and_2_out, not_1_out, not_2_out;

  not not_1 (not_1_out, A);
  not not_2 (not_2_out, B);
  and and_1 (and_1_out, not_1_out, not_2_out);
  and and_2 (and_2_out, B, A);
  or or_1 (out_3, and_1_out, and_2_out);
endmodule

module _4_bit_comparator (
  input  B0,
  input  B1,
  input  B2,
  input  B3,
  input  A0,
  input  A1,
  input  A2,
  input  A3,
  output out_9
);

  wire and_1_out, and_2_out, myxnor_1_out_3, myxnor_2_out_3, myxnor_3_out_3, myxnor_4_out_3;

  MyXNOR myxnor_1 (.A(A3), .B(B3), .out_3(myxnor_1_out_3));
  MyXNOR myxnor_2 (.A(B2), .B(A2), .out_3(myxnor_2_out_3));
  MyXNOR myxnor_3 (.A(B1), .B(A1), .out_3(myxnor_3_out_3));
  MyXNOR myxnor_4 (.A(B0), .B(A0), .out_3(myxnor_4_out_3));
  and and_1 (and_1_out, myxnor_1_out_3, myxnor_2_out_3);
  and and_2 (and_2_out, myxnor_3_out_3, myxnor_4_out_3);
  and and_3 (out_9, and_1_out, and_2_out);
endmodule
