// Logisim project lab02_65070159.circ as structural Verilog: 1 circuit, main circuit main
module main (
  input  A,
  input  B,
  input  C,
  output out_4
);

  wire nand_1_out;

  nand nand_1 (nand_1_out, A, B);
  nand nand_2 (out_4, nand_1_out, C);
endmodule
